# Fritzing sketch schematic (saved by Fritzing 0.9.3b)

parts:
  Mod1 = Raspberry Pi Pico  # not connected
  LCD1 = LCD screen  # not connected
  Driver1 = 28BYJ-48 Driver Module [part_number=ULN2003 package=THT]
  ENCODER1 = Rotary Encoder with switch (KY-040) [part_number=KY-040]  # not connected
  SM1 = 28BYJ-48 Stepper Motor [part_number=28BYJ-48]

nets:
  N1: Driver1.blue-pin, SM1.blue-pin
  N2: Driver1.pink-pin, SM1.pink-pin
  N3: Driver1.yellow-pin, SM1.yellow-pin
  N4: Driver1.orange-pin, SM1.orange-pin
  N5: Driver1.red-pin, SM1.red-pin

custom parts:
  Raspberry Pi Pico: Raspberry Pi Pico. Based around the RP2040 microcontroller the Pico is a low cost microcontroller device bringing Raspberry Pi quality, cost, and easy of use to the microcontroller space. Jan 2021, Split part in to two versions: tht (this one) and SMD. This one will drill holes for a .1 in header in pcb to allow plugging in the module as well as providing pads to solder the module to the top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
  28BYJ-48 Driver Module: ULN2003 Driver Module for the 28BYJ-48 Unipolar Stepper Motor LED A - Blue wire - Bottom coil left LED B - Pink wire - Top coil left LED C - Yellow wire - Bottom coil right LED D - Orange wire - Top coil right Common rail - red Connector pins: blue - pink - yellow - orange - red Control pins - IN1 to IN4 Power pins - GND & Vmotor (5-12V) On/Off jumper (if removed, power to motor is cut).
  Rotary Encoder with switch (KY-040): A Rotary Encoder with switch
  28BYJ-48 Stepper Motor: Unipolar Stepper Motor 28BYJ-48 Top coil - pink & orange Bottom coil - blue & yellow Common rail - red Connector pins: blue - pink - yellow - orange - red
